// Logisim project CPU.circ as structural Verilog: 11 circuits, main circuit ALUExtend1
// AE1
module ALUExtend1 (
  input  a,
  input  b,
  input  [2:0] xyz,
  output ia,
  output ib
);

  wire and_1_out, not_1_out, or_1_out, xor_1_out;
  wire [1:1] or_2_out;

  and and_1 (and_1_out, a, b);
  or or_1 (or_1_out, a, b);
  xor xor_1 (xor_1_out, a, b);
  Multiplexer #(.select(2), .enable("false")) multiplexer_1 (
    .in0(and_1_out), .in1(or_1_out), .in2(a), .in3(xor_1_out), .out(ia), .sel({or_2_out[1], xyz[0]}));
  or or_2 (or_2_out[1], xyz[2], xyz[1]);
  not not_1 (not_1_out, xyz[0]);
  and and_2 (ib, b, not_1_out, xyz[1]);
endmodule

// AE2
module ALUExtend2 (
  input  [1:0] a,
  input  [1:0] b,
  input  [2:0] xyz,
  output [1:0] ia,
  output [1:0] ib
);

  ALUExtend1 aluextend1_1 (.a(a[0]), .b(b[0]), .xyz(xyz), .ia(ia[0]), .ib(ib[0]));
  ALUExtend1 aluextend1_2 (.a(a[1]), .b(b[1]), .xyz(xyz), .ia(ia[1]), .ib(ib[1]));
endmodule

// AE4
module ALUExtend4 (
  input  [3:0] a,
  input  [3:0] b,
  input  [2:0] xyz,
  output [3:0] ia,
  output [3:0] ib
);

  ALUExtend2 aluextend2_1 (.a(a[1:0]), .b(b[1:0]), .xyz(xyz), .ia(ia[1:0]), .ib(ib[1:0]));
  ALUExtend2 aluextend2_2 (.a(a[3:2]), .b(b[3:2]), .xyz(xyz), .ia(ia[3:2]), .ib(ib[3:2]));
endmodule

// AE8
module ALUExtend8 (
  input  [7:0] a,
  input  [7:0] b,
  input  [2:0] xyz,
  output [7:0] ia,
  output [7:0] ib
);

  ALUExtend4 aluextend4_1 (.a(a[3:0]), .b(b[3:0]), .xyz(xyz), .ia(ia[3:0]), .ib(ib[3:0]));
  ALUExtend4 aluextend4_2 (.a(a[7:4]), .b(b[7:4]), .xyz(xyz), .ia(ia[7:4]), .ib(ib[7:4]));
endmodule

module ALU (
  input  [2:0] xyz,
  input  [17:0] a,
  input  [17:0] b,
  output [17:0] out
);

  wire [1:0] aluextend2_1_ia, aluextend2_1_ib;
  wire [7:0] aluextend8_1_ia, aluextend8_1_ib, aluextend8_2_ia, aluextend8_2_ib;

  ALUExtend8 aluextend8_1 (.a(a[7:0]), .b(b[7:0]), .xyz(xyz), .ia(aluextend8_1_ia), .ib(aluextend8_1_ib));
  ALUExtend8 aluextend8_2 (.a(a[15:8]), .b(b[15:8]), .xyz(xyz), .ia(aluextend8_2_ia), .ib(aluextend8_2_ib));
  ALUExtend2 aluextend2_1 (.a(a[17:16]), .b(b[17:16]), .xyz(xyz), .ia(aluextend2_1_ia), .ib(aluextend2_1_ib));
  Adder #(.width(18)) adder_1 (
    .a({aluextend2_1_ia, aluextend8_2_ia, aluextend8_1_ia}),
    .b({aluextend2_1_ib, aluextend8_2_ib, aluextend8_1_ib}), .out(out), .cin(xyz[2]));  // open: cout
endmodule

// RF2
module RegisterFile2 (
  input  rd1,
  input  rd2,
  input  [17:0] \input ,
  input  wd1,
  input  we,
  output [17:0] output1,
  output [17:0] output2
);

  wire not_1_out, not_2_out, not_3_out;
  wire [17:0] R0_q, R1_q;

  Register #(.width(18)) R0 (.D(\input ), .en(not_1_out), .Q(R0_q), .clk(we));  // open: clr
  not not_1 (not_1_out, wd1);
  Register #(.width(18)) R1 (.D(\input ), .en(wd1), .Q(R1_q), .clk(we));  // open: clr
  not not_2 (not_2_out, rd1);
  assign output1 = not_2_out ? R0_q : 18'bz;  // Controlled_Buffer controlled_buffer_1
  not not_3 (not_3_out, rd2);
  assign output2 = not_3_out ? R0_q : 18'bz;  // Controlled_Buffer controlled_buffer_2
  assign output1 = rd1 ? R1_q : 18'bz;  // Controlled_Buffer controlled_buffer_3
  assign output2 = rd2 ? R1_q : 18'bz;  // Controlled_Buffer controlled_buffer_4
endmodule

// RF4
module RegisterFile4 (
  input  [1:0] rd1,
  input  [1:0] rd2,
  input  [17:0] \input ,
  input  [1:0] wd1,
  input  we,
  output [17:0] output1,
  output [17:0] output2
);

  wire controlled_buffer_1_out, controlled_buffer_2_out, not_1_out, not_2_out, not_3_out;
  wire [17:0] registerfile2_1_output1, registerfile2_1_output2, registerfile2_2_output1,
       registerfile2_2_output2;

  not not_1 (not_1_out, wd1[1]);
  assign controlled_buffer_1_out = not_1_out ? we : 1'bz;  // Controlled_Buffer controlled_buffer_1
  assign controlled_buffer_2_out = wd1[1] ? we : 1'bz;  // Controlled_Buffer controlled_buffer_2
  RegisterFile2 registerfile2_1 (
    .rd1(rd1[0]), .rd2(rd2[0]), .\input (\input ), .wd1(wd1[0]), .we(controlled_buffer_1_out),
    .output1(registerfile2_1_output1), .output2(registerfile2_1_output2));
  RegisterFile2 registerfile2_2 (
    .rd1(rd1[0]), .rd2(rd2[0]), .\input (\input ), .wd1(wd1[0]), .we(controlled_buffer_2_out),
    .output1(registerfile2_2_output1), .output2(registerfile2_2_output2));
  not not_2 (not_2_out, rd1[1]);
  assign output1 = not_2_out ? registerfile2_1_output1 : 18'bz;  // Controlled_Buffer controlled_buffer_3
  assign output1 = rd1[1] ? registerfile2_2_output1 : 18'bz;  // Controlled_Buffer controlled_buffer_4
  assign output2 = rd2[1] ? registerfile2_2_output2 : 18'bz;  // Controlled_Buffer controlled_buffer_5
  not not_3 (not_3_out, rd2[1]);
  assign output2 = not_3_out ? registerfile2_1_output2 : 18'bz;  // Controlled_Buffer controlled_buffer_6
endmodule

// RF8
module RegisterFile8 (
  input  [2:0] rd1,
  input  [2:0] rd2,
  input  [17:0] \input ,
  input  [2:0] wd1,
  input  we,
  output [17:0] output1,
  output [17:0] output2
);

  wire controlled_buffer_1_out, controlled_buffer_2_out, not_1_out, not_2_out, not_3_out;
  wire [17:0] registerfile4_1_output1, registerfile4_1_output2, registerfile4_2_output1,
       registerfile4_2_output2;

  assign controlled_buffer_1_out = not_1_out ? we : 1'bz;  // Controlled_Buffer controlled_buffer_1
  not not_1 (not_1_out, wd1[2]);
  assign controlled_buffer_2_out = wd1[2] ? we : 1'bz;  // Controlled_Buffer controlled_buffer_2
  RegisterFile4 registerfile4_1 (
    .rd1(rd1[1:0]), .rd2(rd2[1:0]), .\input (\input ), .wd1(wd1[1:0]), .we(controlled_buffer_1_out),
    .output1(registerfile4_1_output1), .output2(registerfile4_1_output2));
  RegisterFile4 registerfile4_2 (
    .rd1(rd1[1:0]), .rd2(rd2[1:0]), .\input (\input ), .wd1(wd1[1:0]), .we(controlled_buffer_2_out),
    .output1(registerfile4_2_output1), .output2(registerfile4_2_output2));
  not not_2 (not_2_out, rd1[2]);
  assign output1 = not_2_out ? registerfile4_1_output1 : 18'bz;  // Controlled_Buffer controlled_buffer_3
  assign output1 = rd1[2] ? registerfile4_2_output1 : 18'bz;  // Controlled_Buffer controlled_buffer_4
  not not_3 (not_3_out, rd2[2]);
  assign output2 = not_3_out ? registerfile4_1_output2 : 18'bz;  // Controlled_Buffer controlled_buffer_5
  assign output2 = rd2[2] ? registerfile4_2_output2 : 18'bz;  // Controlled_Buffer controlled_buffer_6
endmodule

module RegisterFile16 (
  input  [3:0] rd1,
  input  [3:0] rd2,
  input  [17:0] \input ,
  input  [3:0] wd1,
  input  we,
  output [17:0] output1,
  output [17:0] output2
);

  wire controlled_buffer_1_out, controlled_buffer_2_out, not_1_out, not_2_out, not_3_out;
  wire [17:0] registerfile8_1_output1, registerfile8_1_output2, registerfile8_2_output1,
       registerfile8_2_output2;

  assign controlled_buffer_1_out = not_1_out ? we : 1'bz;  // Controlled_Buffer controlled_buffer_1
  not not_1 (not_1_out, wd1[3]);
  assign controlled_buffer_2_out = wd1[3] ? we : 1'bz;  // Controlled_Buffer controlled_buffer_2
  RegisterFile8 registerfile8_1 (
    .rd1(rd1[2:0]), .rd2(rd2[2:0]), .\input (\input ), .wd1(wd1[2:0]), .we(controlled_buffer_1_out),
    .output1(registerfile8_1_output1), .output2(registerfile8_1_output2));
  RegisterFile8 registerfile8_2 (
    .rd1(rd1[2:0]), .rd2(rd2[2:0]), .\input (\input ), .wd1(wd1[2:0]), .we(controlled_buffer_2_out),
    .output1(registerfile8_2_output1), .output2(registerfile8_2_output2));
  not not_2 (not_2_out, rd1[3]);
  assign output1 = not_2_out ? registerfile8_1_output1 : 18'bz;  // Controlled_Buffer controlled_buffer_3
  assign output1 = rd1[3] ? registerfile8_2_output1 : 18'bz;  // Controlled_Buffer controlled_buffer_4
  not not_3 (not_3_out, rd2[3]);
  assign output2 = not_3_out ? registerfile8_1_output2 : 18'bz;  // Controlled_Buffer controlled_buffer_5
  assign output2 = rd2[3] ? registerfile8_2_output2 : 18'bz;  // Controlled_Buffer controlled_buffer_6
endmodule

module PC (
  input  [17:0] \input ,
  input  we,
  output [17:0] \output 
);

  wire clock_1_out;

  Register #(.width(18)) IR (.D(\input ), .en(we), .Q(\output ), .clk(clock_1_out));  // open: clr
  Clock clock_1 (.out(clock_1_out));
endmodule

module CPU (
);

  ROM #(.addrWidth(18), .dataWidth(18)) rom_1 ();  // open: addr, data, sel
  RAM #(.addrWidth(10), .dataWidth(18), .bus("separate")) ram_1 ();  // open: addr, din, data, str, sel, clk, ld, clr

  // Notes on the sheet:
  //   Instruction Memory
  //   Data Memory
endmodule
